# Fritzing sketch ScriptieDrawing (saved by Fritzing 0.9.3b)
circuit board: 10.6124cm x 6.24843cm
breadboards: 1

parts:
  Microcontroller = Arduino Uno (Rev3)
  LDR = Photocell (LDR) [package=THT]
  Q1 = PNP-Transistor [package="TO92 [THT]"]
  Q2 = PNP-Transistor [package="TO92 [THT]"]
  M1 = DC Motor
  M2 = DC Motor
  VCC2 = Battery block 9V
  VCC1 = Battery block 9V
  D1 = Rectifier Diode [part_number=1N4001 package="300 mil [THT]"]
  D2 = Rectifier Diode [part_number=1N4001 package="300 mil [THT]"]
  LED1 = LED - 5mm [color="White (4500K)" package="5 mm [THT]"]
  R2 = Resistor [tolerance=±5% resistance=220 package=THT]
  HC-SR04_Ultrasonic_Sensor = HC-SR04 Ultrasonic Distance Sensor
  R3 = Resistor [tolerance=±5% resistance=220 package=THT]

nets:
  N1: Microcontroller.A0, R3.Pin_0
  N2: Microcontroller.D8, HC-SR04_Ultrasonic_Sensor.GND
  N3: Microcontroller.GND, VCC2.-, VCC1.-, D1.cathode, D2.cathode, R2.Pin_1, HC-SR04_Ultrasonic_Sensor.ECHO
  N4: Microcontroller.D2, LED1.anode
  N5: Microcontroller.D5_PWM, Q2.B
  N6: Microcontroller.D6_PWM, Q1.B
  N7: Microcontroller.D7, HC-SR04_Ultrasonic_Sensor.TRIG
  5V: Microcontroller.5V, LDR.pin_1, VCC1.+, HC-SR04_Ultrasonic_Sensor.VCC
  N8: LDR.pin_0, R3.Pin_1
  N9: Q1.E, Q2.E, VCC2.+
  N10: Q1.C, M1.pin_1
  N11: Q2.C, M2.pin_1
  N12: M1.pin_2, D1.anode
  N13: M2.pin_2, D2.anode
  N14: LED1.cathode, R2.Pin_0
